// Logisim project CPU-V2.circ as structural Verilog: 3 circuits, main circuit main
module main (
);

  wire ACT, and_1_out, and_2_out, and_3_out, and_4_out, and_5_out, and_6_out, and_7_out, and_8_out,
       and_9_out, and_10_out, and_11_out, and_12_out, COMP_A_ODD, COMP_B_ODD, COMP_EQL, COMP_GT, COMP_LT,
       COMP_NE, decoder_1_out5, decoder_1_out6, decoder_1_out7, decoder_1_out8, INS_ADD, INS_COMPARE,
       INS_JUMP, INS_LOADNUM, INS_MEM2REG, INS_MOVE, INS_NOOP, INS_REG2MEM, INS_SUB, JUMP_EQL, JUMP_GT,
       JUMP_LT, JUMP_NE, JUMP_UN, LOAD, NEXT, or_1_out, or_2_out, PREP, REG_B_ACC, REG_B_GP1, REG_B_GP2,
       REG_B_GP3, REG_B_GP4, REG_C_ACC, REG_C_GP1, REG_C_GP2, REG_C_GP3, REG_C_GP4, register_2_q, SAVE;
  wire [5:2] comparator_1_gt;
  wire [7:0] adder_1_out, adder_2_out, JUMP_ADDR, multiplexer_1_out, multiplexer_2_out, multiplexer_3_out,
       multiplexer_4_out, multiplexer_9_out, multiplexer_14_out, REG_ACC, REG_GP1, REG_GP2, REG_GP3, REG_GP4,
       REG_SRC0, REG_SRC1, REG_SRC2, REG_TARGET, register_1_q, ROM_ADDR, subtractor_1_out;
  wire [15:0] rom_1_data;
  wire [15:8] ROM_DATA;

  // Probe on ROM_ADDR
  // Probe on {ROM_DATA, JUMP_ADDR}
  // Probe on ROM_DATA[15:12]
  // Probe on ROM_DATA[11:8]
  // Probe on JUMP_ADDR[7:4]
  // Probe on JUMP_ADDR[3:0]
  Clock clock_1 (.out_1(PREP), .out_2(LOAD), .out_3(ACT), .out_4(SAVE), .out_5(NEXT));
  and and_1 (and_1_out, INS_JUMP, JUMP_UN);
  and and_2 (and_2_out, INS_JUMP, COMP_EQL, JUMP_EQL);
  and and_3 (and_3_out, INS_JUMP, COMP_LT, JUMP_LT);
  and and_4 (and_4_out, INS_JUMP, COMP_GT, JUMP_GT);
  and and_5 (and_5_out, INS_JUMP, COMP_NE, JUMP_NE);
  Decoder #(.select(4)) decoder_1 (
    .out0(JUMP_UN), .out1(JUMP_EQL), .out2(JUMP_NE), .out3(JUMP_GT), .out4(JUMP_LT), .out5(decoder_1_out5),
    .out6(decoder_1_out6), .out7(decoder_1_out7), .out8(decoder_1_out8), .sel(ROM_DATA[11:8]));  // open: out9, out10, out11, out12, out13, out14, out15, en
  Decoder #(.select(4)) decoder_2 (
    .out0(REG_B_ACC), .out1(REG_B_GP1), .out2(REG_B_GP2), .out3(REG_B_GP3), .out4(REG_B_GP4),
    .sel(JUMP_ADDR[7:4]));  // open: out5, out6, out7, out8, out9, out10, out11, out12, out13, out14, out15, en
  or or_1 (or_1_out, INS_ADD, INS_SUB, INS_LOADNUM, INS_MOVE);
  Multiplexer #(.width(8)) multiplexer_1 (
    .in0(REG_TARGET), .in1(JUMP_ADDR), .out(multiplexer_1_out), .sel(INS_LOADNUM));  // open: en
  // Probe on {ROM_DATA[11:8], JUMP_ADDR[7:4]}
  // Probe on JUMP_ADDR
  or or_2 (or_2_out, and_1_out, and_2_out, and_3_out, and_4_out, and_5_out);
  // Probe on register_1_q
  Adder adder_1 (.a(ROM_ADDR), .b(8'h1), .out(adder_1_out));  // open: cin, cout
  Register register_1 (.D(JUMP_ADDR), .Q(register_1_q), .clk(ACT));  // open: en, clr
  Register #(.width(1)) register_2 (.D(or_2_out), .Q(register_2_q), .clk(ACT));  // open: en, clr
  and and_6 (and_6_out, SAVE, or_1_out, JUMP_UN);
  and and_7 (and_7_out, SAVE, or_1_out, JUMP_EQL);
  and and_8 (and_8_out, SAVE, or_1_out, JUMP_NE);
  and and_9 (and_9_out, SAVE, or_1_out, JUMP_GT);
  and and_10 (and_10_out, SAVE, or_1_out, JUMP_LT);
  Multiplexer #(.width(8)) multiplexer_2 (
    .in0(multiplexer_1_out), .in1(REG_SRC1), .out(multiplexer_2_out), .sel(INS_MOVE));  // open: en
  // Probe on REG_ACC
  // Probe on REG_GP1
  // Probe on REG_GP2
  // Probe on REG_GP3
  // Probe on REG_GP4
  // Probe on multiplexer_3_out
  Multiplexer #(.width(8)) multiplexer_3 (
    .in0(adder_1_out), .in1(register_1_q), .out(multiplexer_3_out), .sel(register_2_q));  // open: en
  Register register_3 (.D(multiplexer_3_out), .Q(ROM_ADDR), .clk(NEXT));  // open: en, clr
  Register register_4 (.D(multiplexer_2_out), .Q(REG_ACC), .clk(and_6_out));  // open: en, clr
  Register register_5 (.D(multiplexer_2_out), .Q(REG_GP1), .clk(and_7_out));  // open: en, clr
  Register register_6 (.D(multiplexer_2_out), .Q(REG_GP2), .clk(and_8_out));  // open: en, clr
  Register register_7 (.D(multiplexer_2_out), .Q(REG_GP3), .clk(and_9_out));  // open: en, clr
  Register register_8 (.D(multiplexer_2_out), .Q(REG_GP4), .clk(and_10_out));  // open: en, clr
  Multiplexer #(.width(8)) multiplexer_4 (.in1(REG_ACC), .out(multiplexer_4_out), .sel(JUMP_UN));  // open: in0, en
  Multiplexer #(.width(8)) multiplexer_5 (.in1(REG_GP1), .out(multiplexer_4_out), .sel(JUMP_EQL));  // open: in0, en
  Multiplexer #(.width(8)) multiplexer_6 (.in1(REG_GP2), .out(multiplexer_4_out), .sel(JUMP_NE));  // open: in0, en
  Multiplexer #(.width(8)) multiplexer_7 (.in1(REG_GP3), .out(multiplexer_4_out), .sel(JUMP_GT));  // open: in0, en
  Multiplexer #(.width(8)) multiplexer_8 (.in1(REG_GP4), .out(multiplexer_4_out), .sel(JUMP_LT));  // open: in0, en
  Decoder #(.select(4)) decoder_3 (
    .out1(INS_NOOP), .out2(INS_MEM2REG), .out3(INS_REG2MEM), .out4(INS_LOADNUM), .out5(INS_MOVE),
    .out6(INS_ADD), .out7(INS_SUB), .out8(INS_COMPARE), .out9(INS_JUMP), .sel(ROM_DATA[15:12]));  // open: out0, out10, out11, out12, out13, out14, out15, en
  Decoder #(.select(4)) decoder_4 (
    .out0(REG_C_ACC), .out1(REG_C_GP1), .out2(REG_C_GP2), .out3(REG_C_GP3), .out4(REG_C_GP4),
    .sel(JUMP_ADDR[3:0]));  // open: out5, out6, out7, out8, out9, out10, out11, out12, out13, out14, out15, en
  Multiplexer #(.width(8)) multiplexer_9 (.in1(REG_ACC), .out(multiplexer_9_out), .sel(REG_B_ACC));  // open: in0, en
  Multiplexer #(.width(8)) multiplexer_10 (.in1(REG_GP1), .out(multiplexer_9_out), .sel(REG_B_GP1));  // open: in0, en
  Multiplexer #(.width(8)) multiplexer_11 (.in1(REG_GP2), .out(multiplexer_9_out), .sel(REG_B_GP2));  // open: in0, en
  Multiplexer #(.width(8)) multiplexer_12 (.in1(REG_GP3), .out(multiplexer_9_out), .sel(REG_B_GP3));  // open: in0, en
  Multiplexer #(.width(8)) multiplexer_13 (.in1(REG_GP4), .out(multiplexer_9_out), .sel(REG_B_GP4));  // open: in0, en
  ROM #(.dataWidth(16)) rom_1 (.addr(ROM_ADDR), .data(rom_1_data), .sel(PREP));
  Register #(.width(16), .trigger("high")) register_9 (
    .D(rom_1_data), .Q({ROM_DATA, JUMP_ADDR}), .clk(PREP));  // open: en, clr
  Multiplexer #(.width(8)) multiplexer_14 (.in1(REG_ACC), .out(multiplexer_14_out), .sel(REG_C_ACC));  // open: in0, en
  Multiplexer #(.width(8)) multiplexer_15 (.in1(REG_GP1), .out(multiplexer_14_out), .sel(REG_C_GP1));  // open: in0, en
  Multiplexer #(.width(8)) multiplexer_16 (.in1(REG_GP2), .out(multiplexer_14_out), .sel(REG_C_GP2));  // open: in0, en
  Multiplexer #(.width(8)) multiplexer_17 (.in1(REG_GP3), .out(multiplexer_14_out), .sel(REG_C_GP3));  // open: in0, en
  Multiplexer #(.width(8)) multiplexer_18 (.in1(REG_GP4), .out(multiplexer_14_out), .sel(REG_C_GP4));  // open: in0, en
  Register register_10 (.D(multiplexer_14_out), .Q(REG_SRC2), .clk(LOAD), .clr(PREP));  // open: en
  Register register_11 (.D(multiplexer_9_out), .Q(REG_SRC1), .clk(LOAD), .clr(PREP));  // open: en
  Register register_12 (.D(multiplexer_4_out), .Q(REG_SRC0), .clk(LOAD), .clr(PREP));  // open: en
  Comparator comparator_1 (
    .a(REG_SRC1), .b(REG_SRC2), .gt(comparator_1_gt[2]), .eq(comparator_1_gt[3]), .lt(comparator_1_gt[4]));
  or or_3 (comparator_1_gt[5], comparator_1_gt[2], comparator_1_gt[4]);
  // Probe on REG_SRC1
  // Probe on REG_SRC2
  // Probe on adder_2_out
  Adder adder_2 (.a(REG_SRC1), .b(REG_SRC2), .out(adder_2_out));  // open: cin, cout
  // Probe on REG_SRC1
  // Probe on REG_SRC2
  // Probe on subtractor_1_out
  Subtractor subtractor_1 (.a(REG_SRC1), .b(REG_SRC2), .out(subtractor_1_out));  // open: bin, bout
  Register #(.width(6)) register_13 (
    .D({comparator_1_gt, REG_SRC1[0], REG_SRC2[0]}),
    .Q({COMP_NE, COMP_LT, COMP_EQL, COMP_GT, COMP_A_ODD, COMP_B_ODD}), .clk(and_11_out), .clr(and_12_out));  // open: en
  and and_11 (and_11_out, INS_COMPARE, SAVE);
  and and_12 (and_12_out, INS_JUMP, NEXT);
  Multiplexer #(.width(8)) multiplexer_19 (
    .in0(adder_2_out), .in1(subtractor_1_out), .out(REG_TARGET), .sel(INS_SUB));  // open: en

  // Other names for the same wires on the sheet: REG_A_ACC = JUMP_UN; REG_A_GP1 = JUMP_EQL; REG_A_GP2 = JUMP_NE;
  //   REG_A_GP3 = JUMP_GT; REG_A_GP4 = JUMP_LT; ROM_INS[3:0] = ROM_DATA[15:12]; ROM_DATA[7:0] = JUMP_ADDR;
  //   ROM_OPT2[3:0] = JUMP_ADDR[7:4]; ROM_OPT4[7:0] = {ROM_DATA[11:8], JUMP_ADDR[7:4]}; ROM_OPT5[7:0] = JUMP_ADDR;
  //   ROM_OPT1[3:0] = ROM_DATA[11:8]; ROM_OPT3[3:0] = JUMP_ADDR[3:0]

  // Notes on the sheet:
  //   5 Stage Clock
  //   Read-only Memory: Contains program binary
  //   contents of rom_1 (hex, n*v repeats v):
  //   4001 4180 4280 8010 9108 6000 900a 9003 5400 9000 7220 9003
  //   Break up 16bit command into components
  //   Arithmetic Logic Unit
endmodule

module Clock (
  output out_1,
  output out_2,
  output out_3,
  output out_4,
  output out_5
);

  wire clock_1_out;
  wire [2:0] counter_1_q;

  Clock_part clock_1 (.out(clock_1_out));
  Counter #(.width(3), .max('h4)) counter_1 (.Q(counter_1_q), .clk(clock_1_out));  // open: load, D, count, carry, clr
  and and_1 (out_1, ~counter_1_q[0], ~counter_1_q[1], ~counter_1_q[2]);  // AND_Gate
  and and_2 (out_2, counter_1_q[0], ~counter_1_q[1], ~counter_1_q[2]);  // AND_Gate
  and and_3 (out_3, ~counter_1_q[0], counter_1_q[1], ~counter_1_q[2]);  // AND_Gate
  and and_4 (out_4, counter_1_q[0], counter_1_q[1], ~counter_1_q[2]);  // AND_Gate
  and and_5 (out_5, ~counter_1_q[0], ~counter_1_q[1], counter_1_q[2]);  // AND_Gate
endmodule

module Controller (
  input  in_1,
  input  in_2,
  input  in_3,
  input  in_4,
  input  [3:0] in_5,
  output out_6,
  output out_7,
  output out_8,
  output out_9,
  output out_10,
  output out_11,
  output out_12,
  output out_13,
  output out_14,
  output out_15
);

  and and_1 (out_6, ~in_1, ~in_2, ~in_3, ~in_4);  // AND_Gate
  and and_2 (out_7, in_1, ~in_2, ~in_3, ~in_4);  // AND_Gate
  and and_3 (out_8, ~in_1, in_2, ~in_3, ~in_4);  // AND_Gate
  and and_4 (out_9, in_1, in_2, ~in_3, ~in_4);  // AND_Gate
  and and_5 (out_10, ~in_1, ~in_2, in_3, ~in_4);  // AND_Gate
  and and_6 (out_11, in_1, ~in_2, in_3, ~in_4);  // AND_Gate
  and and_7 (out_12, ~in_1, in_2, in_3, ~in_4);  // AND_Gate
  and and_8 (out_13, in_1, in_2, in_3, ~in_4);  // AND_Gate
  and and_9 (out_14, ~in_1, ~in_2, ~in_3, in_4);  // AND_Gate
  and and_10 (out_15, in_1, ~in_2, ~in_3, in_4);  // AND_Gate

  assign in_5 = {in_4, in_3, in_2, in_1};
endmodule
